// Logisim project datapath.circ as structural Verilog: 5 circuits, main circuit 1bit adder
module _1bit_adder (
  input  a,
  input  b,
  input  cin,
  output sum,
  output cout
);

  wire and_1_out, and_2_out, xor_1_out;

  xor xor_1 (xor_1_out, a, b);
  xor xor_2 (sum, xor_1_out, cin);
  and and_1 (and_1_out, cin, xor_1_out);
  and and_2 (and_2_out, b, a);
  or or_1 (cout, and_1_out, and_2_out);
endmodule

module _32_bit_ship_right (
  input  [31:0] in_1,
  output [31:0] out_2
);


  assign out_2 = {1'b0, in_1[31:1]};
endmodule

module _32_bit_adder (
  input  [31:0] in_1,
  input  [31:0] in_2,
  output [31:0] out_3
);

  wire n1bit_adder_1_cout, n1bit_adder_2_cout, n1bit_adder_3_cout, n1bit_adder_4_cout, n1bit_adder_5_cout,
       n1bit_adder_6_cout, n1bit_adder_7_cout, n1bit_adder_8_cout, n1bit_adder_9_cout, n1bit_adder_10_cout,
       n1bit_adder_11_cout, n1bit_adder_12_cout, n1bit_adder_13_cout, n1bit_adder_14_cout,
       n1bit_adder_15_cout, n1bit_adder_16_cout, n1bit_adder_17_cout, n1bit_adder_18_cout,
       n1bit_adder_19_cout, n1bit_adder_20_cout, n1bit_adder_21_cout, n1bit_adder_22_cout,
       n1bit_adder_23_cout, n1bit_adder_24_cout, n1bit_adder_25_cout, n1bit_adder_26_cout,
       n1bit_adder_27_cout, n1bit_adder_28_cout, n1bit_adder_29_cout, n1bit_adder_30_cout,
       n1bit_adder_31_cout;

  _1bit_adder u_1bit_adder_1 (.a(in_1[0]), .b(in_2[0]), .cin(1'b0), .sum(out_3[0]), .cout(n1bit_adder_1_cout));
  _1bit_adder u_1bit_adder_2 (
    .a(in_1[1]), .b(in_2[1]), .cin(n1bit_adder_1_cout), .sum(out_3[1]), .cout(n1bit_adder_2_cout));
  _1bit_adder u_1bit_adder_3 (
    .a(in_1[2]), .b(in_2[2]), .cin(n1bit_adder_2_cout), .sum(out_3[2]), .cout(n1bit_adder_3_cout));
  _1bit_adder u_1bit_adder_4 (
    .a(in_1[3]), .b(in_2[3]), .cin(n1bit_adder_3_cout), .sum(out_3[3]), .cout(n1bit_adder_4_cout));
  _1bit_adder u_1bit_adder_5 (
    .a(in_1[4]), .b(in_2[4]), .cin(n1bit_adder_4_cout), .sum(out_3[4]), .cout(n1bit_adder_5_cout));
  _1bit_adder u_1bit_adder_6 (
    .a(in_1[5]), .b(in_2[5]), .cin(n1bit_adder_5_cout), .sum(out_3[5]), .cout(n1bit_adder_6_cout));
  _1bit_adder u_1bit_adder_7 (
    .a(in_1[6]), .b(in_2[6]), .cin(n1bit_adder_6_cout), .sum(out_3[6]), .cout(n1bit_adder_7_cout));
  _1bit_adder u_1bit_adder_8 (
    .a(in_1[7]), .b(in_2[7]), .cin(n1bit_adder_7_cout), .sum(out_3[7]), .cout(n1bit_adder_8_cout));
  _1bit_adder u_1bit_adder_9 (
    .a(in_1[8]), .b(in_2[8]), .cin(n1bit_adder_8_cout), .sum(out_3[8]), .cout(n1bit_adder_9_cout));
  _1bit_adder u_1bit_adder_10 (
    .a(in_1[10]), .b(in_2[10]), .cin(n1bit_adder_11_cout), .sum(out_3[10]), .cout(n1bit_adder_10_cout));
  _1bit_adder u_1bit_adder_11 (
    .a(in_1[9]), .b(in_2[9]), .cin(n1bit_adder_9_cout), .sum(out_3[9]), .cout(n1bit_adder_11_cout));
  _1bit_adder u_1bit_adder_12 (
    .a(in_1[11]), .b(in_2[11]), .cin(n1bit_adder_10_cout), .sum(out_3[11]), .cout(n1bit_adder_12_cout));
  _1bit_adder u_1bit_adder_13 (
    .a(in_1[12]), .b(in_2[12]), .cin(n1bit_adder_12_cout), .sum(out_3[12]), .cout(n1bit_adder_13_cout));
  _1bit_adder u_1bit_adder_14 (
    .a(in_1[13]), .b(in_2[13]), .cin(n1bit_adder_13_cout), .sum(out_3[13]), .cout(n1bit_adder_14_cout));
  _1bit_adder u_1bit_adder_15 (
    .a(in_1[14]), .b(in_2[14]), .cin(n1bit_adder_14_cout), .sum(out_3[14]), .cout(n1bit_adder_15_cout));
  _1bit_adder u_1bit_adder_16 (
    .a(in_1[15]), .b(in_2[15]), .cin(n1bit_adder_15_cout), .sum(out_3[15]), .cout(n1bit_adder_16_cout));
  _1bit_adder u_1bit_adder_17 (
    .a(in_1[16]), .b(in_2[16]), .cin(n1bit_adder_16_cout), .sum(out_3[16]), .cout(n1bit_adder_17_cout));
  _1bit_adder u_1bit_adder_18 (
    .a(in_1[17]), .b(in_2[17]), .cin(n1bit_adder_17_cout), .sum(out_3[17]), .cout(n1bit_adder_18_cout));
  _1bit_adder u_1bit_adder_19 (
    .a(in_1[18]), .b(in_2[18]), .cin(n1bit_adder_18_cout), .sum(out_3[18]), .cout(n1bit_adder_19_cout));
  _1bit_adder u_1bit_adder_20 (
    .a(in_1[19]), .b(in_2[19]), .cin(n1bit_adder_19_cout), .sum(out_3[19]), .cout(n1bit_adder_20_cout));
  _1bit_adder u_1bit_adder_21 (
    .a(in_1[20]), .b(in_2[20]), .cin(n1bit_adder_20_cout), .sum(out_3[20]), .cout(n1bit_adder_21_cout));
  _1bit_adder u_1bit_adder_22 (
    .a(in_1[21]), .b(in_2[21]), .cin(n1bit_adder_21_cout), .sum(out_3[21]), .cout(n1bit_adder_22_cout));
  _1bit_adder u_1bit_adder_23 (
    .a(in_1[22]), .b(in_2[22]), .cin(n1bit_adder_22_cout), .sum(out_3[22]), .cout(n1bit_adder_23_cout));
  _1bit_adder u_1bit_adder_24 (
    .a(in_1[23]), .b(in_2[23]), .cin(n1bit_adder_23_cout), .sum(out_3[23]), .cout(n1bit_adder_24_cout));
  _1bit_adder u_1bit_adder_25 (
    .a(in_1[24]), .b(in_2[24]), .cin(n1bit_adder_24_cout), .sum(out_3[24]), .cout(n1bit_adder_25_cout));
  _1bit_adder u_1bit_adder_26 (
    .a(in_1[25]), .b(in_2[25]), .cin(n1bit_adder_25_cout), .sum(out_3[25]), .cout(n1bit_adder_26_cout));
  _1bit_adder u_1bit_adder_27 (
    .a(in_1[26]), .b(in_2[26]), .cin(n1bit_adder_26_cout), .sum(out_3[26]), .cout(n1bit_adder_27_cout));
  _1bit_adder u_1bit_adder_28 (
    .a(in_1[27]), .b(in_2[27]), .cin(n1bit_adder_27_cout), .sum(out_3[27]), .cout(n1bit_adder_28_cout));
  _1bit_adder u_1bit_adder_29 (
    .a(in_1[28]), .b(in_2[28]), .cin(n1bit_adder_28_cout), .sum(out_3[28]), .cout(n1bit_adder_29_cout));
  _1bit_adder u_1bit_adder_30 (
    .a(in_1[29]), .b(in_2[29]), .cin(n1bit_adder_29_cout), .sum(out_3[29]), .cout(n1bit_adder_30_cout));
  _1bit_adder u_1bit_adder_31 (
    .a(in_1[30]), .b(in_2[30]), .cin(n1bit_adder_30_cout), .sum(out_3[30]), .cout(n1bit_adder_31_cout));
  _1bit_adder u_1bit_adder_32 (.a(in_1[31]), .b(in_2[31]), .cin(n1bit_adder_31_cout), .sum(out_3[31]));  // open: cout
endmodule

module _32_bit_ALU (
  input  [31:0] input1,
  input  in_2,
  input  [31:0] input2,
  output [31:0] out_4
);

  wire [31:0] n32_bit_adder_1_out_3, n32_bit_ship_right_1_out_2;

  _32_bit_adder u_32_bit_adder_1 (.in_1(input1), .in_2(input2), .out_3(n32_bit_adder_1_out_3));
  _32_bit_ship_right u_32_bit_ship_right_1 (.in_1(input1), .out_2(n32_bit_ship_right_1_out_2));
  Multiplexer #(.width(32)) multiplexer_1 (
    .in0(n32_bit_adder_1_out_3), .in1(n32_bit_ship_right_1_out_2), .out(out_4), .sel(in_2));  // open: en
endmodule

module datapath (
  input  [31:0] multiplicand,
  input  [31:0] multiplicand_2,
  input  in_3,
  input  [31:0] multiplier,
  output [31:0] out_5,
  output [31:0] out_6
);

  wire [31:0] multiplexer_1_out, n32_bit_alu_1_out_4, n32_bit_alu_2_out_4, n32_bit_alu_3_out_4,
       n32_bit_ship_right_1_out_2;

  _32_bit_ALU u_32_bit_alu_1 (.input1(multiplicand), .in_2(1'b0), .input2({32{1'b0}}), .out_4(n32_bit_alu_1_out_4));
  _32_bit_ALU u_32_bit_alu_2 (.input1(multiplier), .in_2(1'b1), .out_4(n32_bit_alu_2_out_4));  // open: input2
  Multiplexer #(.width(32)) multiplexer_1 (
    .in0({32{1'b0}}), .in1(32'h80000000), .out(multiplexer_1_out), .sel(out_5[0]));  // open: en
  _32_bit_ALU u_32_bit_alu_3 (
    .input1(n32_bit_alu_1_out_4), .in_2(in_3), .input2(multiplicand_2), .out_4(n32_bit_alu_3_out_4));
  _32_bit_adder u_32_bit_adder_1 (.in_1(n32_bit_alu_2_out_4), .in_2(multiplexer_1_out), .out_3(out_6));
  _32_bit_ship_right u_32_bit_ship_right_1 (.in_1(n32_bit_alu_3_out_4), .out_2(n32_bit_ship_right_1_out_2));
  Multiplexer #(.width(32)) multiplexer_2 (
    .in0(n32_bit_ship_right_1_out_2), .in1(n32_bit_alu_3_out_4), .out(out_5), .sel(in_3));  // open: en
endmodule
