// Logisim project mult32.circ as structural Verilog: 1 circuit, main circuit  mult32
module mult32 (
  input  [31:0] in_1,
  input  [31:0] in_2,
  output [31:0] out_3,
  output [31:0] out_4
);

  wire and_1_out, clock_1_out, datapath_1_p3, or_1_out;
  wire [4:0] counter_1_q;
  wire [31:0] datapath_1_p5, datapath_1_p6, multiplexer_1_out, multiplexer_2_out, register_1_q, register_2_q;

  Counter #(.width(5), .max('h1f)) counter_1 (.Q(counter_1_q), .clk(clock_1_out));  // open: load, D, count, carry, clr
  Clock clock_1 (.out(clock_1_out));
  or or_1 (or_1_out, counter_1_q[4], counter_1_q[3], counter_1_q[2], counter_1_q[1], counter_1_q[0]);
  Multiplexer #(.width(32)) multiplexer_1 (
    .in0(in_1), .in1(register_1_q), .out(multiplexer_1_out), .sel(or_1_out));  // open: en
  Multiplexer #(.width(32)) multiplexer_2 (
    .in0(in_2), .in1(register_2_q), .out(multiplexer_2_out), .sel(or_1_out));  // open: en
  Register #(.width(32)) register_1 (.D(datapath_1_p5), .Q(register_1_q), .clk(clock_1_out));  // open: en, clr
  // datapath datapath_1: pin names not known; wires that end beside it: multiplexer_1_out, in_1, datapath_1_p3, multiplexer_2_out, datapath_1_p5, datapath_1_p6
  control control_1 (.in_1(multiplexer_2_out), .alu(datapath_1_p3));
  Demultiplexer #(.width(32)) demultiplexer_1 (
    .out0(out_4), .out1(out_3), .in(datapath_1_p6), .sel(and_1_out));  // open: en
  and and_1 (and_1_out, counter_1_q[4], counter_1_q[3], counter_1_q[2], counter_1_q[1], counter_1_q[0]);
  Register #(.width(32)) register_2 (.D(out_4), .Q(register_2_q), .clk(clock_1_out));  // open: en, clr
endmodule
